# Fritzing sketch Completo (saved by Fritzing 1.0.4)
breadboards: 2

parts:
  SP1 = SPEAKER [package=pcb_mount_speaker]
  DFRobot_DFPlayer_Mini1 = DFRobot DFPlayer Mini [part_number=DFR0299]
  U1 = LuaNode32 / ESP32 [part_number=ESP32S-PIN30]
  Componente1 = RFID-RC522-v3
  R1 = Resistor [tolerance=±5% resistance=220 package="0805 [SMD]"]
  LED1 = RGB LED (com. cathode, rbg) [color="Red (633nm)" current=0.030A package="5 mm [THT]"]
  R2 = Resistor [tolerance=±5% resistance=330 package="0402 [SMD]"]
  R3 = Resistor [tolerance=±5% resistance=330 package="0402 [SMD]"]
  R4 = Resistor [tolerance=±5% resistance=330 package="0402 [SMD]"]

nets:
  N1: SP1.+, DFRobot_DFPlayer_Mini1.SPK_2
  N2: SP1.-, DFRobot_DFPlayer_Mini1.SPK_1
  VCC: DFRobot_DFPlayer_Mini1.VCC, U1.Vin
  N3: DFRobot_DFPlayer_Mini1.RX, R1.Pin_0
  N4: DFRobot_DFPlayer_Mini1.TX, U1.RX2
  GND: DFRobot_DFPlayer_Mini1.GND-1, DFRobot_DFPlayer_Mini1.GND-2, U1.GND, Componente1.GND, LED1.common_cathode
  N5: U1.D25, R2.Pin_0
  N6: U1.D26, R3.Pin_0
  N7: U1.D27, R4.Pin_0
  3V3: U1.3V3, Componente1.3.3V
  N8: U1.TX2, R1.Pin_1
  N9: U1.D5, Componente1.SDA
  N10: U1.D18, Componente1.SCK
  N11: U1.D19, Componente1.MISO
  N12: U1.D22, Componente1.RST
  N13: U1.D23, Componente1.MOSI
  N14: LED1.red_anode, R2.Pin_1
  N15: LED1.blue_anode, R4.Pin_1
  N16: LED1.green_anode, R3.Pin_1

notes:
  Falta agregar el motor para que "el tocadiscos" gire y sea visual.

custom parts:
  LuaNode32 / ESP32: New Image for LuaNode32 DOIT ESP32 DEVKIT V1. Base parts from LuaNode32 / ESP32 ESP32 based LuaNode32 by G.Noorlander DOIT Esp32 DevKit v1 (30 pins long, 11 pins width) by Werner Rothschopf (modified by vanepp Dec 2018)
  RFID-RC522-v3: A simple China made RFID-RC522 Reader (6x4 cm); do check the pin labels, as this is a MFRC522 based clone.
