# Fritzing sketch DFPlayer (saved by Fritzing 1.0.4)
breadboards: 2

parts:
  U1 = LuaNode32 / ESP32 [part_number=ESP32S-PIN30]
  DFRobot_DFPlayer_Mini1 = DFRobot DFPlayer Mini [part_number=DFR0299]
  SP1 = SPEAKER [package=pcb_mount_speaker]

nets:
  N1: U1.GND, DFRobot_DFPlayer_Mini1.GND-1, DFRobot_DFPlayer_Mini1.GND-2
  VIN: U1.Vin, DFRobot_DFPlayer_Mini1.VCC
  N2: U1.RX2, DFRobot_DFPlayer_Mini1.TX
  N3: DFRobot_DFPlayer_Mini1.SPK_1, SP1.-
  N4: DFRobot_DFPlayer_Mini1.SPK_2, SP1.+

custom parts:
  LuaNode32 / ESP32: New Image for LuaNode32 DOIT ESP32 DEVKIT V1. Base parts from LuaNode32 / ESP32 ESP32 based LuaNode32 by G.Noorlander DOIT Esp32 DevKit v1 (30 pins long, 11 pins width) by Werner Rothschopf (modified by vanepp Dec 2018)
