# Fritzing sketch RFID (saved by Fritzing 1.0.4)
breadboards: 1

parts:
  Componente1 = RFID-RC522-v3
  U1 = LuaNode32 / ESP32 [part_number=ESP32S-PIN30]

nets:
  N1: Componente1.SDA, U1.D5
  N2: Componente1.SCK, U1.D18
  N3: Componente1.MOSI, U1.D23
  N4: Componente1.MISO, U1.D19
  GND: Componente1.GND, U1.GND
  N5: Componente1.RST, U1.D22
  3.3V: Componente1.3.3V, U1.3V3

custom parts:
  RFID-RC522-v3: A simple China made RFID-RC522 Reader (6x4 cm); do check the pin labels, as this is a MFRC522 based clone.
  LuaNode32 / ESP32: New Image for LuaNode32 DOIT ESP32 DEVKIT V1. Base parts from LuaNode32 / ESP32 ESP32 based LuaNode32 by G.Noorlander DOIT Esp32 DevKit v1 (30 pins long, 11 pins width) by Werner Rothschopf (modified by vanepp Dec 2018)
