# Fritzing sketch RGB (saved by Fritzing 1.0.4)
breadboards: 2

parts:
  U1 = LuaNode32 / ESP32 [part_number=ESP32S-PIN30]
  LED2 = RGB LED (com. cathode, rbg) [color="Red (633nm)" current=0.030A package="5 mm [THT]"]
  R1 = Resistor [tolerance=±5% resistance=330 package="1206 [SMD]"]
  R2 = Resistor [tolerance=±5% resistance=330 package="1206 [SMD]"]
  R3 = Resistor [tolerance=±5% resistance=330 package="1206 [SMD]"]

nets:
  N1: U1.D25, R1.Pin_1
  N2: U1.D26, R2.Pin_1
  N3: U1.D27, R3.Pin_1
  N4: U1.GND, LED2.common_cathode
  N5: LED2.red_anode, R1.Pin_0
  N6: LED2.blue_anode, R3.Pin_0
  N7: LED2.green_anode, R2.Pin_0

custom parts:
  LuaNode32 / ESP32: New Image for LuaNode32 DOIT ESP32 DEVKIT V1. Base parts from LuaNode32 / ESP32 ESP32 based LuaNode32 by G.Noorlander DOIT Esp32 DevKit v1 (30 pins long, 11 pins width) by Werner Rothschopf (modified by vanepp Dec 2018)
